// Logisim project ALU .circ as structural Verilog: 5 circuits, main circuit ALU 1bit
module ALU_1bit (
  input  Data_IN_B,
  input  Data_IN_A,
  input  Carry_In,
  input  Binvert,
  input  [3:0] Operation,
  output Data_0,
  output Carry0
);

  wire adder_1_out, and_1_out, multiplexer_1_out, not_1_out, not_2_out, not_3_out, or_1_out;

  not not_1 (not_1_out, Data_IN_B);
  Multiplexer multiplexer_1 (.in0(Data_IN_B), .in1(not_1_out), .out(multiplexer_1_out), .sel(Binvert));  // open: en
  and and_1 (and_1_out, Data_IN_A, Data_IN_B);
  or or_1 (or_1_out, Data_IN_A, Data_IN_B);
  Adder #(.width(1)) adder_1 (.a(Data_IN_A), .b(multiplexer_1_out), .out(adder_1_out), .cin(Carry_In), .cout(Carry0));
  not not_2 (not_2_out, and_1_out);
  not not_3 (not_3_out, or_1_out);
  Multiplexer #(.select(4)) multiplexer_2 (
    .in0(adder_1_out), .in1(adder_1_out), .in2(not_2_out), .in3(or_1_out), .in4(not_3_out), .in6(Data_IN_A),
    .in7(Data_IN_A), .in8(adder_1_out), .in12(adder_1_out), .out(Data_0), .sel(Operation));  // open: in5, in9, in10, in11, in13, in14, in15, en
endmodule

// ALU
module ALU_16_bit (
  input  [15:0] Data_IN_B,
  input  Carry_In,
  input  [15:0] Data_IN_A,
  input  [3:0] shamt,
  input  [3:0] Operation,
  input  Binvert,
  output LESS,
  output [15:0] Data,
  output Overflow,
  output Carry_1
);

  wire alu_0_1_carry0, alu_1bit_1_carry0, alu_1bit_2_carry0, alu_1bit_3_carry0, alu_1bit_4_carry0,
       alu_1bit_5_carry0, alu_1bit_6_carry0, alu_1bit_7_carry0, alu_1bit_8_carry0, alu_1bit_9_carry0,
       alu_1bit_10_carry0, alu_1bit_11_carry0, alu_1bit_12_carry0, alu_1bit_13_carry0, alu_1bit_14_carry0,
       alu_15_1_set;
  wire [15:0] alu_0_1_data_0, shifter_1_out, shifter_2_out;

  ALU_1bit alu_1bit_1 (
    .Data_0(alu_0_1_data_0[1]), .Carry0(alu_1bit_1_carry0), .Data_IN_B(Data_IN_B[1]),
    .Data_IN_A(Data_IN_A[1]), .Carry_In(alu_0_1_carry0), .Binvert(Binvert), .Operation(Operation));
  ALU_1bit alu_1bit_2 (
    .Data_0(alu_0_1_data_0[2]), .Carry0(alu_1bit_2_carry0), .Data_IN_B(Data_IN_B[2]),
    .Data_IN_A(Data_IN_A[2]), .Carry_In(alu_1bit_1_carry0), .Binvert(Binvert), .Operation(Operation));
  ALU_1bit alu_1bit_3 (
    .Data_0(alu_0_1_data_0[3]), .Carry0(alu_1bit_3_carry0), .Data_IN_B(Data_IN_B[3]),
    .Data_IN_A(Data_IN_A[3]), .Carry_In(alu_1bit_2_carry0), .Binvert(Binvert), .Operation(Operation));
  ALU_1bit alu_1bit_4 (
    .Data_0(alu_0_1_data_0[4]), .Carry0(alu_1bit_4_carry0), .Data_IN_B(Data_IN_B[4]),
    .Data_IN_A(Data_IN_A[4]), .Carry_In(alu_1bit_3_carry0), .Binvert(Binvert), .Operation(Operation));
  ALU_1bit alu_1bit_5 (
    .Data_0(alu_0_1_data_0[5]), .Carry0(alu_1bit_5_carry0), .Data_IN_B(Data_IN_B[5]),
    .Data_IN_A(Data_IN_A[5]), .Carry_In(alu_1bit_4_carry0), .Binvert(Binvert), .Operation(Operation));
  ALU_1bit alu_1bit_6 (
    .Data_0(alu_0_1_data_0[6]), .Carry0(alu_1bit_6_carry0), .Data_IN_B(Data_IN_B[6]),
    .Data_IN_A(Data_IN_A[6]), .Carry_In(alu_1bit_5_carry0), .Binvert(Binvert), .Operation(Operation));
  ALU_1bit alu_1bit_7 (
    .Data_0(alu_0_1_data_0[7]), .Carry0(alu_1bit_7_carry0), .Data_IN_B(Data_IN_B[7]),
    .Data_IN_A(Data_IN_A[7]), .Carry_In(alu_1bit_6_carry0), .Binvert(Binvert), .Operation(Operation));
  ALU_1bit alu_1bit_8 (
    .Data_0(alu_0_1_data_0[8]), .Carry0(alu_1bit_8_carry0), .Data_IN_B(Data_IN_B[8]),
    .Data_IN_A(Data_IN_A[8]), .Carry_In(alu_1bit_7_carry0), .Binvert(Binvert), .Operation(Operation));
  ALU_1bit alu_1bit_9 (
    .Data_0(alu_0_1_data_0[9]), .Carry0(alu_1bit_9_carry0), .Data_IN_B(Data_IN_B[9]),
    .Data_IN_A(Data_IN_A[9]), .Carry_In(alu_1bit_8_carry0), .Binvert(Binvert), .Operation(Operation));
  ALU_1bit alu_1bit_10 (
    .Data_0(alu_0_1_data_0[10]), .Carry0(alu_1bit_10_carry0), .Data_IN_B(Data_IN_B[10]),
    .Data_IN_A(Data_IN_A[10]), .Carry_In(alu_1bit_9_carry0), .Binvert(Binvert), .Operation(Operation));
  ALU_1bit alu_1bit_11 (
    .Data_0(alu_0_1_data_0[11]), .Carry0(alu_1bit_11_carry0), .Data_IN_B(Data_IN_B[11]),
    .Data_IN_A(Data_IN_A[11]), .Carry_In(alu_1bit_10_carry0), .Binvert(Binvert), .Operation(Operation));
  ALU_1bit alu_1bit_12 (
    .Data_0(alu_0_1_data_0[12]), .Carry0(alu_1bit_12_carry0), .Data_IN_B(Data_IN_B[12]),
    .Data_IN_A(Data_IN_A[12]), .Carry_In(alu_1bit_11_carry0), .Binvert(Binvert), .Operation(Operation));
  ALU_1bit alu_1bit_13 (
    .Data_0(alu_0_1_data_0[13]), .Carry0(alu_1bit_13_carry0), .Data_IN_B(Data_IN_B[13]),
    .Data_IN_A(Data_IN_A[13]), .Carry_In(alu_1bit_12_carry0), .Binvert(Binvert), .Operation(Operation));
  ALU_1bit alu_1bit_14 (
    .Data_0(alu_0_1_data_0[14]), .Carry0(alu_1bit_14_carry0), .Data_IN_B(Data_IN_B[14]),
    .Data_IN_A(Data_IN_A[14]), .Carry_In(alu_1bit_13_carry0), .Binvert(Binvert), .Operation(Operation));
  ALU_15 alu_15_1 (
    .Data_0(alu_0_1_data_0[15]), .CarryOut(Carry_1), .Data_IN_B(Data_IN_B[15]), .Data_IN_A(Data_IN_A[15]),
    .Carry_In(alu_1bit_14_carry0), .Binvert(Binvert), .Operation(Operation), .SET(alu_15_1_set));
  ALU_0 alu_0_1 (
    .Data_0(alu_0_1_data_0[0]), .LESS(LESS), .Carry0(alu_0_1_carry0), .DATA_IN_B(Data_IN_B[0]),
    .Data_IN_A(Data_IN_A[0]), .Carry_In(Carry_In), .Binvert(Binvert), .Operation(Operation),
    .SET(alu_15_1_set));
  xor xor_1 (Overflow, alu_1bit_14_carry0, Carry_1);
  Shifter #(.width(16)) shifter_1 (.in(alu_0_1_data_0), .\dist (shamt), .out(shifter_1_out));
  Shifter #(.width(16), .shift("lr")) shifter_2 (.in(alu_0_1_data_0), .\dist (shamt), .out(shifter_2_out));
  Multiplexer #(.select(4), .width(16)) multiplexer_1 (
    .in0(alu_0_1_data_0), .in1(alu_0_1_data_0), .in2(alu_0_1_data_0), .in3(alu_0_1_data_0),
    .in4(alu_0_1_data_0), .in5(alu_0_1_data_0), .in6(shifter_1_out), .in7(shifter_2_out),
    .in8(alu_0_1_data_0), .in9(alu_0_1_data_0), .in10(alu_0_1_data_0), .in11(alu_0_1_data_0),
    .in12(alu_0_1_data_0), .in13(alu_0_1_data_0), .in14(alu_0_1_data_0), .in15(alu_0_1_data_0), .out(Data),
    .sel(Operation));  // open: en

  // Notes on the sheet:
  //   ALU 1
  //   2
  //   3
  //   4
  //   5
  //   6
  //   7
  //   8
  //   9
  //   10
  //   11
  //   12
  //   13
  //   14
  //   ALU 0
  //   ALU15
endmodule

module ALU (
  input  [15:0] Data_IN_A,
  input  Carry_In,
  input  [15:0] DATA_IN_B,
  input  [3:0] Operation,
  input  Binvert,
  input  [3:0] in_6,
  output OverFlow,
  output Carry_1,
  output [15:0] Data,
  output LESS
);

  ALU_16_bit alu_16_bit_1 (
    .Operation(Operation), .Binvert(Binvert), .Carry_1(Carry_1), .Data_IN_B(DATA_IN_B),
    .Data_IN_A(Data_IN_A), .Carry_In(Carry_In), .Data(Data), .LESS(LESS), .Overflow(OverFlow), .shamt(in_6));

  // Notes on the sheet:
  //   Shamt
endmodule

module ALU_0 (
  input  DATA_IN_B,
  input  Data_IN_A,
  input  Carry_In,
  input  SET,
  input  Binvert,
  input  [3:0] Operation,
  output Data_0,
  output LESS,
  output Carry0
);

  wire adder_1_out, and_1_out, multiplexer_1_out, not_1_out, not_2_out, not_3_out, or_1_out;

  not not_1 (not_1_out, DATA_IN_B);
  Multiplexer multiplexer_1 (.in0(DATA_IN_B), .in1(not_1_out), .out(multiplexer_1_out), .sel(Binvert));  // open: en
  and and_1 (and_1_out, Data_IN_A, DATA_IN_B);
  or or_1 (or_1_out, Data_IN_A, DATA_IN_B);
  Adder #(.width(1)) adder_1 (.a(Data_IN_A), .b(multiplexer_1_out), .out(adder_1_out), .cin(Carry_In), .cout(Carry0));
  not not_2 (not_2_out, and_1_out);
  not not_3 (not_3_out, or_1_out);
  Multiplexer #(.select(4)) multiplexer_2 (
    .in0(adder_1_out), .in1(adder_1_out), .in2(not_2_out), .in3(or_1_out), .in4(not_3_out),
    .in5(adder_1_out), .in6(Data_IN_A), .in7(Data_IN_A), .in8(adder_1_out), .in12(adder_1_out), .out(Data_0),
    .sel(Operation));  // open: in9, in10, in11, in13, in14, in15, en

  assign LESS = SET;
endmodule

module ALU_15 (
  input  Data_IN_B,
  input  Data_IN_A,
  input  Carry_In,
  input  Binvert,
  input  [3:0] Operation,
  output Data_0,
  output SET,
  output CarryOut
);

  wire adder_1_out, and_1_out, multiplexer_1_out, not_1_out, not_2_out, not_3_out, or_1_out;

  not not_1 (not_1_out, Data_IN_B);
  Multiplexer multiplexer_1 (.in0(Data_IN_B), .in1(not_1_out), .out(multiplexer_1_out), .sel(Binvert));  // open: en
  and and_1 (and_1_out, Data_IN_A, Data_IN_B);
  or or_1 (or_1_out, Data_IN_A, Data_IN_B);
  Adder #(.width(1)) adder_1 (.a(Data_IN_A), .b(multiplexer_1_out), .out(adder_1_out), .cin(Carry_In), .cout(CarryOut));
  not not_2 (not_2_out, and_1_out);
  not not_3 (not_3_out, or_1_out);
  Multiplexer #(.select(4)) multiplexer_2 (
    .in0(adder_1_out), .in1(adder_1_out), .in2(not_2_out), .in3(or_1_out), .in4(not_3_out),
    .in5(adder_1_out), .in6(Data_IN_A), .in7(Data_IN_A), .in8(adder_1_out), .in12(adder_1_out), .out(Data_0),
    .sel(Operation));  // open: in9, in10, in11, in13, in14, in15, en

  assign SET = Data_0;
endmodule
