// Logisim project cur.circ as structural Verilog: 1 circuit, main circuit main
module main (
  input  in_1,
  input  in_2
);

  wire and_1_out, and_2_out, not_1_out, not_2_out, or_1_out;

  not not_1 (not_1_out, in_1);
  not not_2 (not_2_out, in_2);
  and and_1 (and_1_out, not_1_out, in_2);
  and and_2 (and_2_out, in_1, in_2);
  or or_1 (or_1_out, not_2_out, and_1_out);
  _7_Segment_Display u_7_segment_display_1 (
    .g(not_1_out), .f(not_2_out), .a(or_1_out), .b(in_1), .e(or_1_out), .d(or_1_out), .c(and_2_out));  // open: dp
endmodule
