// Logisim project datapath.circ as structural Verilog: 3 circuits, main circuit main
module main (
  input  in_1,
  input  CarryIn,
  input  [15:0] Data_Input,
  input  [3:0] in_4,
  input  Overflow
);

  wire alu_16_bit_1_carry_1, alu_contrl_1_cin, and_1_out, clock_1_out, main_control_1_aluop0,
       main_control_1_aluop1, main_control_1_alusrc, main_control_1_branch, main_control_1_memread,
       main_control_1_memwrite, main_control_1_rdst, main_control_1_regwrite, main_control_1_shi;
  wire [3:0] multiplexer_1_out, undriven, undriven_2;
  wire [15:0] adder_1_out, adder_2_out, alu_16_bit_1_data, bit_extender_1_out, bit_extender_2_out,
       main_1_out1, main_1_out2, multiplexer_2_out, multiplexer_3_out, multiplexer_4_out, multiplexer_5_out,
       ram_1_data, register_1_q, rom_1_data, shifter_1_out;

  Clock clock_1 (.out(clock_1_out));
  Register #(.width(16)) register_1 (.D(adder_1_out), .Q(register_1_q), .clk(clock_1_out));  // open: en, clr
  Adder #(.width(16)) adder_1 (.a(Data_Input), .b(register_1_q), .out(adder_1_out), .cin(in_1));  // open: cout
  ROM #(.addrWidth(16), .dataWidth(16)) rom_1 (
    .addr(register_1_q), .data({rom_1_data[15:14], rom_1_data[15:14], rom_1_data[11:0]}));  // open: sel
  main_control main_control_1 (
    .SHIFT(rom_1_data[8]), .OPcode(rom_1_data[11:9]), .Shi(main_control_1_shi), .Rdst(main_control_1_rdst),
    .ALUOp0(main_control_1_aluop0), .ALUsrc(main_control_1_alusrc), .Branch(main_control_1_branch),
    .ALUop1(main_control_1_aluop1), .MemRead(main_control_1_memread), .MemWrite(main_control_1_memwrite),
    .RegWrite(main_control_1_regwrite));  // open: MemToReg
  Multiplexer #(.width(4)) multiplexer_1 (
    .in0({rom_1_data[7], rom_1_data[5:3]}), .in1({rom_1_data[6], rom_1_data[2:0]}), .out(multiplexer_1_out),
    .sel(main_control_1_aluop0));  // open: en
  assign bit_extender_1_out = {{15{1'b0}}, rom_1_data[8]};  // Bit_Extender bit_extender_1
  RegisterFile_main main_1 (
    .In(multiplexer_5_out), .Rs({rom_1_data[7], rom_1_data[5:3]}), .Rt(multiplexer_1_out), .Rd(undriven_2),
    .in_5(clock_1_out), .Out1(main_1_out1), .Out2(main_1_out2));
  assign bit_extender_2_out = {{9{1'b0}}, {rom_1_data[15:14], rom_1_data[6], rom_1_data[8], rom_1_data[2:0]}};  // Bit_Extender bit_extender_2
  Multiplexer #(.width(16)) multiplexer_2 (
    .in0(main_1_out2), .in1(bit_extender_2_out), .out(multiplexer_2_out), .sel(main_control_1_shi));  // open: en
  Multiplexer #(.width(16)) multiplexer_3 (
    .in0(multiplexer_2_out), .in1(bit_extender_1_out), .out(multiplexer_3_out), .sel(main_control_1_memwrite));  // open: en
  Shifter #(.width(16)) shifter_1 (.in(bit_extender_2_out), .\dist (in_4), .out(shifter_1_out));
  ALU_16_bit alu_16_bit_1 (
    .Operation(undriven_2), .Binvert(alu_contrl_1_cin), .Carry_1(alu_16_bit_1_carry_1),
    .Data_IN_B(multiplexer_3_out), .Data_IN_A(main_1_out1), .Carry_In(CarryIn), .Data(alu_16_bit_1_data),
    .Overflow(Overflow), .shamt(undriven));  // open: LESS
  alu_contrl alu_contrl_1 (
    .OPCODE(rom_1_data[11:9]), .ALU0p1(main_control_1_rdst), .ALUOp0(main_control_1_branch),
    .Binvert(CarryIn), .OPERATION(undriven), .Cin(alu_contrl_1_cin));
  Adder #(.width(16)) adder_2 (.a(adder_1_out), .b(shifter_1_out), .out(adder_2_out));  // open: cin, cout
  Multiplexer #(.width(16)) multiplexer_4 (
    .in0(bit_extender_2_out), .in1(adder_2_out), .out(multiplexer_4_out), .sel(and_1_out));  // open: en
  and and_1 (and_1_out, main_control_1_alusrc, alu_16_bit_1_carry_1);
  RAM #(.addrWidth(16), .dataWidth(16)) ram_1 (
    .addr(alu_16_bit_1_data), .data(ram_1_data), .sel(main_control_1_aluop1), .clk(clock_1_out),
    .ld(main_control_1_memread));  // open: clr
  Multiplexer #(.width(16)) multiplexer_5 (
    .in0(ram_1_data), .in1(alu_16_bit_1_data), .out(multiplexer_5_out), .sel(main_control_1_regwrite));  // open: en
  Multiplexer #(.width(16)) multiplexer_6 (
    .in0(multiplexer_4_out), .in1(bit_extender_2_out), .out(adder_1_out));  // open: sel, en
endmodule

module main_control (
  input  SHIFT,
  input  [2:0] OPcode,
  output Shi,
  output Rdst,
  output ALUOp0,
  output ALUsrc,
  output Branch,
  output ALUop1,
  output MemRead,
  output MemWrite,
  output RegWrite,
  output MemToReg
);

  wire and_3_out, not_1_out, not_2_out;

  and and_1 (MemWrite, OPcode[1], not_1_out);
  and and_2 (ALUop1, OPcode[2], OPcode[1]);
  not not_1 (not_1_out, OPcode[0]);
  not not_2 (not_2_out, OPcode[2]);
  and and_3 (and_3_out, not_2_out, not_1_out);
  not not_3 (ALUOp0, OPcode[1]);
  and and_4 (MemRead, OPcode[1], not_1_out);
  and and_5 (MemToReg, OPcode[1], not_2_out);
  and and_6 (ALUsrc, OPcode[1], not_2_out);
  or or_1 (RegWrite, ALUOp0, and_3_out);
  and and_7 (Shi, SHIFT, 1'b0);

  assign Branch = ALUop1;
  assign Rdst = ALUOp0;
endmodule

module alu_contrl (
  input  Binvert,
  input  [3:0] OPERATION,
  input  [2:0] OPCODE,
  input  ALU0p1,
  input  ALUOp0,
  output Cin
);

  wire decoder_1_out1, decoder_1_out2, decoder_1_out5, decoder_1_out8, decoder_1_out16;

  Decoder #(.select(5)) decoder_1 (
    .out1(decoder_1_out1), .out2(decoder_1_out2), .out3(OPERATION[0]), .out4(OPERATION[1]),
    .out5(decoder_1_out5), .out8(decoder_1_out8), .out16(decoder_1_out16), .sel({ALUOp0, ALU0p1, OPCODE}));  // open: out0, out6, out7, out9, out10, out11, out12, out13, out14, out15, out17, out18, out19, out20, out21, out22, out23, out24, out25, out26, out27, out28, out29, out30, out31, en
  or or_1 (Binvert, decoder_1_out1, decoder_1_out16);
  or or_2 (Cin, decoder_1_out1, decoder_1_out16);
  or or_3 (OPERATION[2], OPERATION[1], decoder_1_out5);
  or or_4 (OPERATION[3], decoder_1_out2, decoder_1_out1, decoder_1_out8, decoder_1_out16);
endmodule
